// Digital circuit downcounter.dig as structural Verilog
module downcounter (
  input  _1_kHz
);

  wire PRESET_out, RST_out, START_out, u_counter_endd, u_counter_test_countdown, u_counter_test_load,
       u_counter_test_start, u_downcounter_zero;
  wire [3:0] dipswitch_1_out, dipswitch_5_out, dipswitch_9_out, dipswitch_13_out, u_downcounter_m1,
       u_downcounter_m10, u_downcounter_s1, u_downcounter_s10;

  Button #(.activeLow("true")) RST (.out(RST_out));
  Seven_Seg_Hex seven_seg_hex_1 (.d(u_downcounter_m10), .dp(1'b0));
  DipSwitch dipswitch_1 (.out(dipswitch_1_out[3]));
  DipSwitch dipswitch_2 (.out(dipswitch_1_out[2]));
  DipSwitch dipswitch_3 (.out(dipswitch_1_out[1]));
  Seven_Seg_Hex seven_seg_hex_2 (.d(u_downcounter_m1), .dp(1'b1));
  downcounter #(.applicationType("IVERILOG")) u_downcounter (
    .rst(RST_out), .c1khz(_1_kHz), .count(u_counter_test_countdown), .load(u_counter_test_load),
    .pm10(dipswitch_1_out), .pm1(dipswitch_5_out), .ps10(dipswitch_9_out), .ps1(dipswitch_13_out),
    .m10(u_downcounter_m10), .m1(u_downcounter_m1), .s10(u_downcounter_s10), .s1(u_downcounter_s1),
    .zero(u_downcounter_zero));
  DipSwitch dipswitch_4 (.out(dipswitch_1_out[0]));
  DipSwitch dipswitch_5 (.out(dipswitch_5_out[3]));
  DipSwitch dipswitch_6 (.out(dipswitch_5_out[2]));
  Seven_Seg_Hex seven_seg_hex_3 (.d(u_downcounter_s10), .dp(1'b0));
  DipSwitch dipswitch_7 (.out(dipswitch_5_out[1]));
  DipSwitch dipswitch_8 (.out(dipswitch_5_out[0]));
  DipSwitch dipswitch_9 (.out(dipswitch_9_out[3]));
  Seven_Seg_Hex seven_seg_hex_4 (.d(u_downcounter_s1), .dp(1'b0));
  DipSwitch dipswitch_10 (.out(dipswitch_9_out[2]));
  DipSwitch dipswitch_11 (.out(dipswitch_9_out[1]));
  DipSwitch dipswitch_12 (.out(dipswitch_9_out[0]));
  DipSwitch dipswitch_13 (.out(dipswitch_13_out[3]));
  DipSwitch dipswitch_14 (.out(dipswitch_13_out[2]));
  DipSwitch dipswitch_15 (.out(dipswitch_13_out[1]));
  DipSwitch dipswitch_16 (.out(dipswitch_13_out[0]));
  counter_test #(.applicationType("IVERILOG")) u_counter_test (
    .clk(_1_kHz), .rst(RST_out), .beginn(START_out), .reset(PRESET_out), .zero(u_downcounter_zero),
    .endd(u_counter_endd), .load(u_counter_test_load), .start(u_counter_test_start),
    .countdown(u_counter_test_countdown));
  Button START (.out(START_out));
  Button PRESET (.out(PRESET_out));
  counter #(.applicationType("IVERILOG")) u_counter (
    .rst(RST_out), .clk(_1_kHz), .start(u_counter_test_start), .endd(u_counter_endd));

  // Notes on the sheet:
  //   _1_kHz: Hz: 1000
endmodule

/* Code of downcounter:
module downcounter(
    input rst, c1khz,
    input count, load, 
    input [3:0] pm10,
    input [3:0] pm1,
    input [3:0] ps10,
    input [3:0] ps1,
    output reg [3:0] m10,
    output reg [3:0] m1,
    output reg [3:0] s10,
    output reg [3:0] s1,
    output zero);
    
    assign zero = ((s1 == 0) && (s10 == 0) && (m1 == 0) && (m10 == 0));
  always @(posedge c1khz, negedge rst)
	begin
      if(rst == 0)
      begin
          s1 <= 0;
          s10 <=0;
          m1 <= 0;
          m10 <= 0;
      end
	
	else 
	begin
      if(load == 1) 
      begin
        s1 <= ps1;
        s10 <= ps10;
        m1 <=  pm1;
        m10 <= pm10;
      end
        else if (count == 1 )
        begin
          if(s1 == 0)
            begin
              s1 = 9;
              if (s10 == 0)
                begin
              	  s10 = 9;
                  if (m1 == 0)
                    begin 
                      m1 = 9;
                      m10 = m10 - 1;
                    end
                  else
                    begin
                      m1 = m1 - 1;
                    end
                end
              else 
                begin 
                  s10 = s10 - 1;
                end
            end
          else
            begin
              s1 = s1-1;
            end
      
        end
    end
    end
	
	
					
					


endmodule
*/

/* Code of counter_test:
module counter_test (
  input clk,
  input rst,
  input beginn,
  input reset,
  input zero,
  input endd,
  output load,
  output start,
  output countdown 
);

  assign start = ((beginn | endd) );
  assign load = reset;
  assign countdown  = (endd && ~zero);
endmodule
*/

/* Code of counter:
module counter(
    input rst,
    input clk,
    input start,
    output endd);
    
    reg [9:0] cnt;
    
    assign endd = (cnt==0);
    
    always @(posedge clk, negedge rst)
    begin
        if (~rst)
        begin
            cnt <= 0;
        end
        else
        begin
            if (start)
                cnt <= 999;
            else if (~endd)
                cnt <= cnt-1;
        end
    end // always
endmodule
*/
